// Logisim project ContadorAmaya.circ as structural Verilog: 1 circuit, main circuit main
module main (
);

  wire and_1_out, and_2_out, and_3_out, button_1_out, j_k_ff_1_q, j_k_ff_2_q, j_k_ff_3_q, n7447_1_pin6,
       n7447_1_pin9, n7447_1_pin10, n7447_1_pin11, n7447_1_pin12, n7447_1_pin13, n7447_1_pin14, n7447_1_pin15;

  J_K_Flip_Flop #(.trigger("falling")) j_k_ff_1 (
    .J(1'b1), .K(1'b1), .clk(button_1_out), .Q(j_k_ff_1_q));  // open: Qn, preset, reset
  Button button_1 (.out(button_1_out));
  J_K_Flip_Flop #(.trigger("falling")) j_k_ff_2 (
    .J(j_k_ff_1_q), .K(j_k_ff_1_q), .clk(button_1_out), .Q(j_k_ff_2_q), .reset(and_3_out));  // open: Qn, preset
  and and_1 (and_1_out, j_k_ff_1_q, j_k_ff_2_q);
  J_K_Flip_Flop #(.trigger("falling")) j_k_ff_3 (
    .J(and_1_out), .K(and_1_out), .clk(button_1_out), .Q(j_k_ff_3_q), .reset(and_3_out));  // open: Qn, preset
  _7447 u_7447_1 (
    .pin1(j_k_ff_2_q), .pin2(j_k_ff_3_q), .pin6(n7447_1_pin6), .pin7(j_k_ff_1_q), .pin15(n7447_1_pin15),
    .pin14(n7447_1_pin14), .pin13(n7447_1_pin13), .pin12(n7447_1_pin12), .pin11(n7447_1_pin11),
    .pin10(n7447_1_pin10), .pin9(n7447_1_pin9));  // open: pin3, pin4, pin5
  and and_2 (and_2_out, j_k_ff_1_q, j_k_ff_2_q, j_k_ff_3_q);
  J_K_Flip_Flop #(.trigger("falling")) j_k_ff_4 (
    .J(and_2_out), .K(and_2_out), .clk(button_1_out), .Q(n7447_1_pin6), .reset(and_3_out));  // open: Qn, preset
  and and_3 (and_3_out, n7447_1_pin6, j_k_ff_2_q);
  _7_Segment_Display #(.active("false")) u_7_segment_display_1 (
    .g(n7447_1_pin14), .f(n7447_1_pin15), .a(n7447_1_pin13), .b(n7447_1_pin12), .e(n7447_1_pin9),
    .d(n7447_1_pin10), .c(n7447_1_pin11));  // open: dp

  // Notes on the sheet:
  //   A
  //   B
  //   C
  //   D
endmodule
