// Logisim project Introduccion_a_logisim-evolution.circ as structural Verilog: 1 circuit, main circuit main
module main (
  input  A,
  input  B,
  input  C,
  input  p,
  input  q,
  input  Sensor_de_RPM,
  input  AA,
  input  BB,
  input  CC,
  input  DD,
  input  EE,
  input  AAA,
  input  BBB,
  input  A1,
  input  B1,
  input  C1,
  input  A2,
  input  B2,
  input  C2
);

  wire and_1_out, and_2_out, and_3_out, and_4_out, and_5_out, and_6_out, and_7_out, and_8_out, nand_1_out,
       nand_2_out, nand_3_out, nor_1_out, nor_2_out, nor_3_out, nor_4_out, not_1_out, not_2_out, not_3_out,
       not_4_out, not_5_out, not_6_out, not_7_out, not_8_out, not_9_out, not_10_out, or_1_out, or_2_out,
       or_3_out, or_4_out;

  not not_1 (not_1_out, C);
  not not_2 (not_2_out, Sensor_de_RPM);
  not not_3 (not_3_out, AA);
  not not_4 (not_4_out, AAA);
  not not_5 (not_5_out, BBB);
  not not_6 (not_6_out, A1);
  and and_1 (and_1_out, B1, C1);
  and and_2 (and_2_out, A2, B2);
  not not_7 (not_7_out, C2);
  not not_8 (not_8_out, BB);
  not not_9 (not_9_out, EE);
  and and_3 (and_3_out, and_2_out, not_7_out);
  nor nor_1 (nor_1_out, A, B);
  nor nor_2 (nor_2_out, B, not_1_out);
  or or_1 (or_1_out, q, not_2_out);
  nand nand_1 (nand_1_out, not_3_out, BB);
  nand nand_2 (nand_2_out, not_8_out, CC);
  and and_4 (and_4_out, AAA, BBB);
  and and_5 (and_5_out, not_4_out, not_5_out);
  nor nor_3 (nor_3_out, not_6_out, and_1_out);
  and and_6 (and_6_out, A1, B1);
  LED led_1 (.in(and_3_out));
  nand nand_3 (nand_3_out, nor_1_out, nor_2_out);
  LED led_2 (.in(nand_3_out));
  and and_7 (and_7_out, p, or_1_out);
  LED led_3 (.in(and_7_out));
  or or_2 (or_2_out, nand_1_out, nand_2_out);
  or or_3 (or_3_out, DD, not_9_out);
  nor nor_4 (nor_4_out, and_4_out, and_5_out);
  and and_8 (and_8_out, nor_3_out, and_6_out);
  LED X1 (.in(and_8_out));
  or or_4 (or_4_out, or_2_out, or_3_out);
  not not_10 (not_10_out, nor_4_out);
  LED led_4 (.in(not_10_out));
  LED led_5 (.in(or_4_out));

  // Notes on the sheet:
  //   Ejercicio 1
  //   Sensor de temperatura
  //   Sensor de presión
  //   Ejercicio 4
  //   Ejercicio 5
  //   Ejercicio 2
  //   r
  //   Ejercicio 3
  //   Luz de advertencia
endmodule
