// Logisim project Reloj.circ as structural Verilog: 1 circuit, main circuit main
module main (
);

  wire A1, a1_t, A2, a2_t, and_1_out, B1, b1_t, B2, b2_t, C1, c1_t, C2, c2_t, CARRY, CU, D1, d1_t, D2, d2_t,
       e1, e2, f1, f2, g1, g2, n74192_1_pin4, n74192_1_pin11, n74192_1_pin14, n74192_2_pin4, n74192_2_pin11;

  Button button_1 (.out(CU));
  and and_1 (and_1_out, C2, B2);
  _74192 u_74192_1 (
    .pin2(B1), .pin3(A1), .pin4(n74192_1_pin4), .pin5(CU), .pin6(C1), .pin7(D1), .pin14(n74192_1_pin14),
    .pin13(CARRY), .pin11(n74192_1_pin11));  // open: pin1, pin15, pin12, pin10, pin9
  _74192 u_74192_2 (
    .pin2(B2), .pin3(A2), .pin4(n74192_2_pin4), .pin5(CARRY), .pin6(C2), .pin7(D2), .pin14(and_1_out),
    .pin11(n74192_2_pin11));  // open: pin1, pin15, pin13, pin12, pin10, pin9
  _7_Segment_Display #(.active("false")) u_7_segment_display_1 (
    .g(g2), .f(f2), .a(a2_t), .b(b2_t), .e(e2), .d(d2_t), .c(c2_t));  // open: dp
  _7_Segment_Display #(.active("false")) u_7_segment_display_2 (
    .g(g1), .f(f1), .a(a1_t), .b(b1_t), .e(e1), .d(d1_t), .c(c1_t));  // open: dp
  _7447 u_7447_1 (
    .pin1(B1), .pin2(C1), .pin6(D1), .pin7(A1), .pin15(f1), .pin14(g1), .pin13(a1_t), .pin12(b1_t),
    .pin11(c1_t), .pin10(d1_t), .pin9(e1));  // open: pin3, pin4, pin5
  _7447 u_7447_2 (
    .pin1(B2), .pin2(C2), .pin6(D2), .pin7(A2), .pin15(f2), .pin14(g2), .pin13(a2_t), .pin12(b2_t),
    .pin11(c2_t), .pin10(d2_t), .pin9(e2));  // open: pin3, pin4, pin5
  // also tied to GND on the sheet: n74192_1_pin14
  // also tied to VCC on the sheet: {n74192_2_pin11, n74192_1_pin11, n74192_2_pin4, n74192_1_pin4}

  // Notes on the sheet:
  //   Load
  //   Clear
  //   Load
  //   Clear
  //   Cout down
  //   Cout down
endmodule
