// Logisim project Sumador_completo_de_5_bits.circ as structural Verilog: 2 circuits, main circuit main
module main (
  input  Suma0,
  input  Cinco0,
  input  Ocho0,
  input  in_4,
  input  in_5,
  input  in_6,
  input  in_7,
  input  in_8,
  input  in_9,
  input  in_10,
  input  in_11,
  input  in_12,
  input  in_13,
  input  Suma1,
  input  Diez1,
  input  Cinco1,
  input  in_17,
  input  in_18,
  input  in_19,
  input  in_20,
  input  in_21,
  input  in_22,
  input  in_23,
  input  in_24,
  input  in_25,
  input  in_26,
  input  Suma2,
  input  Doce2,
  input  Ocho2,
  input  in_30,
  input  in_31,
  input  in_32,
  input  in_33,
  input  in_34,
  input  in_35,
  input  in_36,
  input  in_37,
  input  in_38,
  input  in_39,
  input  Suma3,
  input  Veinte3,
  input  Veinte33,
  input  in_43,
  input  in_44,
  input  in_45,
  input  in_46,
  input  in_47,
  input  in_48,
  input  in_49,
  input  in_50,
  input  in_51,
  input  in_52,
  input  in_53,
  input  in_54,
  input  in_55,
  input  in_56,
  input  in_57,
  input  in_58,
  input  in_59,
  input  in_60,
  input  in_61,
  input  in_62,
  input  in_63,
  input  in_64,
  input  in_65,
  output out_66,
  output out_67,
  output out_68,
  output out_69,
  output out_70,
  output out_71,
  output out_72,
  output out_73,
  output out_74,
  output out_75,
  output out_76,
  output out_77,
  output out_78,
  output out_79,
  output out_80,
  output out_81,
  output out_82,
  output out_83,
  output out_84,
  output out_85,
  output out_86,
  output out_87,
  output out_88,
  output out_89,
  output out_90,
  output out_91,
  output out_92,
  output out_93
);

  wire fa_6_out_5, fa_7_out_5, fa_8_out_5, fa_9_out_5, fa_10_out_5, fa_11_out_5, fa_12_out_5, fa_13_out_5,
       fa_14_out_5, fa_15_out_5, fa_16_out_5, fa_17_out_5, fa_18_out_5, fa_19_out_5, fa_20_out_5,
       fa_21_out_5, fa_22_out_5, fa_23_out_5, fa_24_out_5, fa_25_out_5;

  FA fa_1 (.A(in_9), .B(in_4), .Cin(fa_6_out_5), .out_4(out_66));  // open: out_5
  FA fa_2 (.A(in_22), .B(in_17), .Cin(fa_7_out_5), .out_4(out_71));  // open: out_5
  FA fa_3 (.A(in_35), .B(in_30), .Cin(fa_8_out_5), .out_4(out_77), .out_5(out_76));
  FA fa_4 (.A(in_48), .B(in_43), .Cin(fa_9_out_5), .out_4(out_83), .out_5(out_82));
  FA fa_5 (.A(in_61), .B(in_56), .Cin(fa_10_out_5), .out_4(out_89), .out_5(out_88));
  FA fa_6 (.A(in_10), .B(in_5), .Cin(fa_11_out_5), .out_4(out_67), .out_5(fa_6_out_5));
  FA fa_7 (.A(in_23), .B(in_18), .Cin(fa_12_out_5), .out_4(out_72), .out_5(fa_7_out_5));
  FA fa_8 (.A(in_36), .B(in_31), .Cin(fa_13_out_5), .out_4(out_78), .out_5(fa_8_out_5));
  FA fa_9 (.A(in_49), .B(in_44), .Cin(fa_14_out_5), .out_4(out_84), .out_5(fa_9_out_5));
  FA fa_10 (.A(in_62), .B(in_57), .Cin(fa_15_out_5), .out_4(out_90), .out_5(fa_10_out_5));
  FA fa_11 (.A(in_11), .B(in_6), .Cin(fa_16_out_5), .out_4(out_68), .out_5(fa_11_out_5));
  FA fa_12 (.A(in_24), .B(in_19), .Cin(fa_17_out_5), .out_4(out_73), .out_5(fa_12_out_5));
  FA fa_13 (.A(in_37), .B(in_32), .Cin(fa_18_out_5), .out_4(out_79), .out_5(fa_13_out_5));
  FA fa_14 (.A(in_50), .B(in_45), .Cin(fa_19_out_5), .out_4(out_85), .out_5(fa_14_out_5));
  FA fa_15 (.A(in_63), .B(in_58), .Cin(fa_20_out_5), .out_4(out_91), .out_5(fa_15_out_5));
  FA fa_16 (.A(in_12), .B(in_7), .Cin(fa_21_out_5), .out_4(out_69), .out_5(fa_16_out_5));
  FA fa_17 (.A(in_25), .B(in_20), .Cin(fa_22_out_5), .out_4(out_74), .out_5(fa_17_out_5));
  FA fa_18 (.A(in_38), .B(in_33), .Cin(fa_23_out_5), .out_4(out_80), .out_5(fa_18_out_5));
  FA fa_19 (.A(in_51), .B(in_46), .Cin(fa_24_out_5), .out_4(out_86), .out_5(fa_19_out_5));
  FA fa_20 (.A(in_64), .B(in_59), .Cin(fa_25_out_5), .out_4(out_92), .out_5(fa_20_out_5));
  FA fa_21 (.A(in_13), .B(in_8), .out_4(out_70), .out_5(fa_21_out_5));  // open: Cin
  FA fa_22 (.A(in_26), .B(in_21), .out_4(out_75), .out_5(fa_22_out_5));  // open: Cin
  FA fa_23 (.A(in_39), .B(in_34), .out_4(out_81), .out_5(fa_23_out_5));  // open: Cin
  FA fa_24 (.A(in_52), .B(in_47), .out_4(out_87), .out_5(fa_24_out_5));  // open: Cin
  FA fa_25 (.A(in_65), .B(in_60), .out_4(out_93), .out_5(fa_25_out_5));  // open: Cin
endmodule

module FA (
  input  A,
  input  B,
  input  Cin,
  output out_4,
  output out_5
);

  wire and_1_out, and_2_out, and_3_out, xor_1_out;

  and and_1 (and_1_out, B, Cin);
  and and_2 (and_2_out, B, A);
  and and_3 (and_3_out, Cin, A);
  xor xor_1 (xor_1_out, B, Cin);
  xor xor_2 (out_4, A, xor_1_out);
  or or_1 (out_5, and_1_out, and_2_out, and_3_out);
endmodule
